// Logisim project DigitalComputerElectronics.circ as structural Verilog
module SR_Latch (
);

  wire CLK, nor_1_out, nor_2_out, RST_out, s_r_ff_1_q, s_r_ff_1_qn, s_r_ff_2_q, s_r_ff_2_qn, SET_out;

  Clock clock_1 (.out(CLK));
  Button RST (.out(RST_out));
  Button SET (.out(SET_out));
  nor nor_1 (nor_1_out, RST_out, nor_2_out);
  nor nor_2 (nor_2_out, nor_1_out, SET_out);
  S_R_Flip_Flop s_r_ff_1 (
    .S(SET_out), .R(RST_out), .clk(CLK), .Q(s_r_ff_1_q), .Qn(s_r_ff_1_qn));  // open: reset, preset
  S_R_Flip_Flop s_r_ff_2 (
    .S(SET_out), .clk(CLK), .R(RST_out), .Q(s_r_ff_2_q), .Qn(s_r_ff_2_qn));  // open: preset, reset
  LED Q1 (.in(nor_1_out));
  LED NQ1 (.in(nor_2_out));
  LED Q2 (.in(s_r_ff_1_q));
  LED NQ2 (.in(s_r_ff_1_qn));
  LED Q3 (.in(s_r_ff_2_q));
  LED NQ3 (.in(s_r_ff_2_qn));
endmodule
